# Fritzing sketch basic_buildup (saved by Fritzing 0.9.2b)
breadboards: 1

parts:
  Bauteil1 = Arduino Yun
  ADC_HX711 = HX711 Weighing Sensor Module
  Raspberry_Pi1 = Raspberry Pi 2  # not connected
  Load_cell_H30A = IC, DIP package, 4 pins [chip_label=H30A]

nets:
  N1: Bauteil1.D0/RX, ADC_HX711.DO/RX
  N2: Bauteil1.D1/TX, ADC_HX711.CK/TX
  5V: Bauteil1.5V, ADC_HX711.VCC
  GND: Bauteil1.GND, ADC_HX711.GND
  N3: ADC_HX711.E+, Load_cell_H30A.pin3
  N4: ADC_HX711.E-, Load_cell_H30A.pin4
  N5: ADC_HX711.A+, Load_cell_H30A.pin2
  N6: ADC_HX711.A-, Load_cell_H30A.pin1

notes:
  http/json
